// Logisim project stcok_predictor.circ as structural Verilog: 1 circuit, main circuit main
module main (
  input  [15:0] in_1,
  output [11:0] program_counter,
  output [7:0] out_3
);

  wire and_1_out, and_2_out, clock_1_out, clock_2_out, clock_3_out, comparator_1_gt, comparator_2_gt,
       not_1_out, not_2_out, t_ff_1_qn, t_ff_2_qn, t_ff_3_qn, t_ff_4_qn, t_ff_5_qn, t_ff_6_qn, t_ff_7_qn,
       t_ff_9_q, t_ff_9_qn, t_ff_10_qn, t_ff_11_q, t_ff_12_q, t_ff_13_qn, t_ff_14_qn;
  wire [9:0] undriven;

  T_Flip_Flop t_ff_1 (.T(1'b1), .clk(clock_1_out), .Q(program_counter[0]), .Qn(t_ff_1_qn));  // open: reset, preset
  Clock clock_1 (.out(clock_1_out));
  T_Flip_Flop t_ff_2 (.T(1'b1), .clk(t_ff_1_qn), .Q(program_counter[1]), .Qn(t_ff_2_qn));  // open: reset, preset
  T_Flip_Flop t_ff_3 (.T(1'b1), .clk(t_ff_2_qn), .Q(program_counter[2]), .Qn(t_ff_3_qn));  // open: reset, preset
  T_Flip_Flop t_ff_4 (.T(1'b1), .clk(t_ff_3_qn), .Q(program_counter[3]), .Qn(t_ff_4_qn));  // open: reset, preset
  T_Flip_Flop t_ff_5 (.T(1'b1), .clk(t_ff_4_qn), .Q(program_counter[4]), .Qn(t_ff_5_qn));  // open: reset, preset
  T_Flip_Flop t_ff_6 (.T(1'b1), .clk(t_ff_5_qn), .Q(program_counter[5]), .Qn(t_ff_6_qn));  // open: reset, preset
  T_Flip_Flop t_ff_7 (.T(1'b1), .clk(t_ff_6_qn), .Q(program_counter[6]), .Qn(t_ff_7_qn));  // open: reset, preset
  not not_1 (not_1_out, comparator_1_gt);
  Comparator #(.width(12)) comparator_1 (.a(program_counter), .b(12'hc8), .gt(comparator_1_gt));  // open: eq, lt
  Clock clock_2 (.out(clock_2_out));
  not not_2 (not_2_out, comparator_2_gt);
  Comparator #(.width(12)) comparator_2 (.a(program_counter), .b(12'h64), .gt(comparator_2_gt));  // open: eq, lt
  T_Flip_Flop t_ff_8 (.T(1'b1), .clk(t_ff_7_qn), .Q(program_counter[7]));  // open: Qn, reset, preset
  T_Flip_Flop t_ff_9 (.T(1'b1), .clk(clock_2_out), .Q(t_ff_9_q), .Qn(t_ff_9_qn), .reset(and_1_out));  // open: preset
  T_Flip_Flop t_ff_10 (
    .T(1'b1), .clk(program_counter[7]), .Q(program_counter[8]), .Qn(t_ff_10_qn));  // open: reset, preset
  T_Flip_Flop t_ff_11 (.T(1'b1), .clk(t_ff_9_qn), .Q(t_ff_11_q), .reset(and_1_out));  // open: Qn, preset
  T_Flip_Flop t_ff_12 (.T(1'b1), .clk(clock_2_out), .Q(t_ff_12_q));  // open: Qn, reset, preset
  T_Flip_Flop t_ff_13 (.T(1'b1), .clk(t_ff_10_qn), .Q(program_counter[9]), .Qn(t_ff_13_qn));  // open: reset, preset
  and and_1 (and_1_out, t_ff_9_q, t_ff_11_q);
  and and_2 (and_2_out, not_1_out, t_ff_12_q);
  Comparator #(.width(10)) comparator_3 (.a(program_counter[9:0]), .b(undriven));  // open: gt, eq, lt
  // AND_Gate and_3 has open pins: in0=not_2_out, in1=and_1_out, out=open
  T_Flip_Flop t_ff_14 (.T(1'b1), .clk(t_ff_13_qn), .Q(program_counter[10]), .Qn(t_ff_14_qn));  // open: reset, preset
  Multiplexer #(.width(8)) multiplexer_1 ();  // open: in0, in1, out, sel
  Multiplexer #(.width(8)) multiplexer_2 (.sel(and_2_out));  // open: in0, in1, out
  T_Flip_Flop t_ff_15 (.T(1'b1), .clk(t_ff_14_qn), .Q(program_counter[11]));  // open: Qn, reset, preset
  RAM #(.addrWidth(10)) ram_1 (.clk(clock_3_out));  // open: addr, we, oe, din, dout
  Clock clock_3 (.out(clock_3_out));
  Register c_1 ();  // open: D, en, clk, Q, clr
  Register c_200 ();  // open: D, en, clk, Q, clr

  assign out_3 = in_1[15:8];
endmodule
